# Fritzing sketch Untitled Sketch (saved by Fritzing 0.9.2b)

parts:
  Eleman1 = Arduino Uno (Rev3)
  J1 = Basic Servo
  VCC1 = Battery block 9V

nets:
  N1: Eleman1.D9_PWM, J1.pulse
  GND: Eleman1.GND, J1.gnd, VCC1.-
