# Fritzing sketch Untitled Sketch (saved by Fritzing 0.9.2b)
breadboards: 1

parts:
  Eleman1 = Arduino Uno (Rev3)
  J1 = Basic Servo
  R1 = Rotary Potentiometer (Small) [maximum_resistance=100kΩ package=THT]

nets:
  N1: Eleman1.A0, R1.wiper
  GND: Eleman1.GND, J1.gnd, R1.leg1
  N2: Eleman1.D3_PWM, J1.pulse
  5V: Eleman1.5V, J1.vcc, R1.leg2
